// Logisim project Lab4.circ as structural Verilog
module adder (
  input  A,
  input  B,
  input  C_in,
  output S,
  output C_out
);

  wire and_1_out, and_2_out, and_3_out, and_4_out, and_5_out, and_6_out, and_7_out, not_1_out, not_2_out,
       not_3_out;

  not not_1 (not_1_out, A);
  not not_2 (not_2_out, B);
  not not_3 (not_3_out, C_in);
  and and_1 (and_1_out, not_1_out, not_2_out, C_in);
  and and_2 (and_2_out, not_1_out, B, not_3_out);
  and and_3 (and_3_out, A, not_2_out, not_3_out);
  and and_4 (and_4_out, A, B, C_in);
  and and_5 (and_5_out, B, C_in);
  and and_6 (and_6_out, A, C_in);
  and and_7 (and_7_out, A, B);
  or or_1 (S, and_1_out, and_2_out, and_3_out, and_4_out);
  or or_2 (C_out, and_5_out, and_6_out, and_7_out);
endmodule

module ALU (
  input  [3:0] in_1,
  input  A,
  input  B,
  input  C_in,
  output S,
  output C_out
);

  wire adder_1_s, and_1_out, multiplexer_1_out, not_1_out, or_1_out, xor_1_out;

  Multiplexer #(.enable("false")) multiplexer_1 (.in0(B), .in1(not_1_out), .out(multiplexer_1_out), .sel(in_1[2]));
  not not_1 (not_1_out, B);
  adder adder_1 (.A(A), .B(multiplexer_1_out), .C_in(C_in), .S(adder_1_s), .C_out(C_out));
  and and_1 (and_1_out, A, multiplexer_1_out);
  or or_1 (or_1_out, A, multiplexer_1_out);
  xor xor_1 (xor_1_out, A, multiplexer_1_out);
  Multiplexer #(.disabled("Z"), .enable("false"), .select(2)) multiplexer_2 (
    .in0(and_1_out), .in1(or_1_out), .in2(xor_1_out), .in3(adder_1_s), .out(S), .sel(in_1[1:0]));
endmodule

module fourALU (
  input  [3:0] in_1,
  input  [3:0] A,
  input  [3:0] B,
  input  C_in,
  output [3:0] out_5,
  output C_out
);

  wire alu_2_c_out, alu_3_c_out, undriven, undriven_2;

  ALU alu_1 (.in_1(in_1), .A(A[0]), .B(A[0]), .C_in(A[3]), .S(out_5[0]), .C_out(out_5[3]));
  ALU alu_2 (.in_1(in_1), .A(A[1]), .B(undriven_2), .C_in(out_5[3]), .S(out_5[1]), .C_out(alu_2_c_out));
  ALU alu_3 (.in_1(in_1), .A(A[2]), .B(A[3]), .C_in(alu_2_c_out), .S(out_5[2]), .C_out(alu_3_c_out));
  ALU alu_4 (.in_1(in_1), .A(A[3]), .B(undriven), .C_in(alu_3_c_out), .S(out_5[3]), .C_out(C_out));

  assign C_in = A[3];
endmodule

module fullALU (
  input  [3:0] in_1,
  input  [35:0] A,
  input  [35:0] B,
  input  C_in,
  output [35:0] S,
  output C_out
);

  wire fouralu_1_c_out, fouralu_2_c_out, fouralu_3_c_out, fouralu_4_c_out, fouralu_5_c_out, fouralu_6_c_out,
       fouralu_7_c_out, fouralu_8_c_out;

  fourALU fouralu_1 (.in_1(A[3:0]), .A(A[3:0]), .B(A[3:0]), .C_in(C_in), .out_5(S[3:0]), .C_out(fouralu_1_c_out));
  fourALU fouralu_2 (
    .in_1(A[3:0]), .A(A[7:4]), .B(A[23:20]), .C_in(fouralu_1_c_out), .out_5(S[7:4]), .C_out(fouralu_2_c_out));
  fourALU fouralu_3 (
    .in_1(A[3:0]), .A(A[35:32]), .B(B[11:8]), .C_in(fouralu_2_c_out), .out_5(S[11:8]), .C_out(fouralu_3_c_out));
  fourALU fouralu_4 (
    .in_1(A[3:0]), .A(A[15:12]), .B(B[15:12]), .C_in(fouralu_3_c_out), .out_5(S[15:12]),
    .C_out(fouralu_4_c_out));
  fourALU fouralu_5 (
    .in_1(A[3:0]), .A(A[19:16]), .B(B[19:16]), .C_in(fouralu_4_c_out), .out_5(S[19:16]),
    .C_out(fouralu_5_c_out));
  fourALU fouralu_6 (
    .in_1(A[3:0]), .A(A[23:20]), .B(A[15:12]), .C_in(fouralu_5_c_out), .out_5(S[27:24]),
    .C_out(fouralu_6_c_out));
  fourALU fouralu_7 (
    .in_1(A[3:0]), .A(A[27:24]), .B(B[27:24]), .C_in(fouralu_6_c_out), .out_5(S[27:24]),
    .C_out(fouralu_7_c_out));
  fourALU fouralu_8 (
    .in_1(A[3:0]), .A(A[31:28]), .B(B[31:28]), .C_in(fouralu_7_c_out), .out_5(S[31:28]),
    .C_out(fouralu_8_c_out));
  fourALU fouralu_9 (
    .in_1(A[3:0]), .A(A[35:32]), .B(B[35:32]), .C_in(fouralu_8_c_out), .out_5(S[35:32]), .C_out(C_out));

  assign A[11:8] = A[35:32];
  assign {B[23:20], B[7:0]} = {A[15:12], A[23:20], A[3:0]};
  assign in_1 = A[3:0];
  assign S[23:20] = S[27:24];
endmodule
